# Fritzing sketch 8-BitAdder (saved by Fritzing 1.0.7)
breadboards: 5

parts:
  Q1 = NPN-Transistor [package="TO92 [THT]"]
  R1 = Resistor [tolerance=±5% power=0.25W resistance=10 package=THT]
  R3 = Resistor [tolerance=±5% power=0.25W resistance=10 package=THT]
  VCC2 = 4 x AAA Battery Mount [internal_resistance=0.1Ω]
  S2 = Toggle Switch [package=THT]
  S3 = Toggle Switch [package=THT]
  S4 = Toggle Switch [package=THT]
  S5 = Toggle Switch [package=THT]
  S6 = Toggle Switch [package=THT]
  S7 = Toggle Switch [package=THT]
  S11 = Toggle Switch [package=THT]
  S12 = Toggle Switch [package=THT]
  S13 = Toggle Switch [package=THT]
  S14 = Toggle Switch [package=THT]
  S15 = Toggle Switch [package=THT]
  S16 = Toggle Switch [package=THT]
  S17 = Toggle Switch [package=THT]
  Q2 = NPN-Transistor [package="TO92 [THT]"]
  Q3 = NPN-Transistor [package="TO92 [THT]"]
  R5 = Resistor [tolerance=±5% power=0.25W resistance=10k package=THT]
  R6 = Resistor [tolerance=±5% power=0.25W resistance=10k package=THT]
  Q4 = NPN-Transistor [package="TO92 [THT]"]
  Q6 = NPN-Transistor [package="TO92 [THT]"]
  Q7 = NPN-Transistor [package="TO92 [THT]"]
  R8 = Resistor [tolerance=±5% power=0.25W resistance=4.7k package=THT]
  R9 = Resistor [tolerance=±5% power=0.25W resistance=4.7k package=THT]
  R10 = Resistor [tolerance=±5% power=0.25W resistance=4.7k package=THT]
  Q5 = NPN-Transistor [package="TO92 [THT]"]
  R13 = Resistor [tolerance=±5% power=0.25W resistance=10k package=THT]
  R14 = Resistor [tolerance=±5% power=0.25W resistance=10k package=THT]
  R15 = Resistor [tolerance=±5% power=0.25W resistance=10k package=THT]
  R16 = Resistor [tolerance=±5% power=0.25W resistance=10k package=THT]
  R17 = Resistor [tolerance=±5% power=0.25W resistance=4.7k package=THT]
  Q8 = NPN-Transistor [package="TO92 [THT]"]
  Q9 = NPN-Transistor [package="TO92 [THT]"]
  Q10 = NPN-Transistor [package="TO92 [THT]"]
  Q11 = NPN-Transistor [package="TO92 [THT]"]
  Q12 = NPN-Transistor [package="TO92 [THT]"]
  Q13 = NPN-Transistor [package="TO92 [THT]"]
  R18 = Resistor [tolerance=±5% power=0.25W resistance=4.7k package=THT]
  R19 = Resistor [tolerance=±5% power=0.25W resistance=4.7k package=THT]
  R20 = Resistor [tolerance=±5% power=0.25W resistance=10k package=THT]
  R21 = Resistor [tolerance=±5% power=0.25W resistance=10k package=THT]
  Q14 = NPN-Transistor [package="TO92 [THT]"]
  Q15 = NPN-Transistor [package="TO92 [THT]"]
  Q16 = NPN-Transistor [package="TO92 [THT]"]
  R22 = Resistor [tolerance=±5% power=0.25W resistance=10k package=THT]
  R23 = Resistor [tolerance=±5% power=0.25W resistance=4.7k package=THT]
  R24 = Resistor [tolerance=±5% power=0.25W resistance=10k package=THT]
  R25 = Resistor [tolerance=±5% power=0.25W resistance=4.7k package=THT]
  R26 = Resistor [tolerance=±5% power=0.25W resistance=10k package=THT]
  Q17 = NPN-Transistor [package="TO92 [THT]"]
  Q18 = NPN-Transistor [package="TO92 [THT]"]
  R27 = Resistor [tolerance=±5% power=0.25W resistance=10k package=THT]
  R28 = Resistor [tolerance=±5% power=0.25W resistance=10k package=THT]
  R29 = Resistor [tolerance=±5% power=0.25W resistance=10k package=THT]
  Q19 = NPN-Transistor [package="TO92 [THT]"]
  R30 = Resistor [tolerance=±5% power=0.25W resistance=4.7k package=THT]
  R31 = Resistor [tolerance=±5% power=0.25W resistance=4.7k package=THT]
  Q20 = NPN-Transistor [package="TO92 [THT]"]
  Q21 = NPN-Transistor [package="TO92 [THT]"]
  Q22 = NPN-Transistor [package="TO92 [THT]"]
  R32 = Resistor [tolerance=±5% power=0.25W resistance=10k package=THT]
  R33 = Resistor [tolerance=±5% power=0.25W resistance=10k package=THT]
  R34 = Resistor [tolerance=±5% power=0.25W resistance=10k package=THT]
  R35 = Resistor [tolerance=±5% power=0.25W resistance=10k package=THT]
  R36 = Resistor [tolerance=±5% power=0.25W resistance=4.7k package=THT]
  R37 = Resistor [tolerance=±5% power=0.25W resistance=4.7k package=THT]
  Q23 = NPN-Transistor [package="TO92 [THT]"]
  Q24 = NPN-Transistor [package="TO92 [THT]"]
  Q25 = NPN-Transistor [package="TO92 [THT]"]
  Q26 = NPN-Transistor [package="TO92 [THT]"]
  Q27 = NPN-Transistor [package="TO92 [THT]"]
  Q28 = NPN-Transistor [package="TO92 [THT]"]
  R38 = Resistor [tolerance=±5% power=0.25W resistance=10k package=THT]
  R39 = Resistor [tolerance=±5% power=0.25W resistance=10k package=THT]
  R40 = Resistor [tolerance=±5% power=0.25W resistance=4.7k package=THT]
  R41 = Resistor [tolerance=±5% power=0.25W resistance=4.7k package=THT]
  R42 = Resistor [tolerance=±5% power=0.25W resistance=4.7k package=THT]
  R43 = Resistor [tolerance=±5% power=0.25W resistance=10k package=THT]
  R44 = Resistor [tolerance=±5% power=0.25W resistance=10k package=THT]
  R45 = Resistor [tolerance=±5% power=0.25W resistance=450 package=THT]
  LED1 = LED - 5mm [color="Red (633nm)" current=0.030A package="5 mm [THT]"]
  Q29 = NPN-Transistor [package="TO92 [THT]"]
  Q30 = NPN-Transistor [package="TO92 [THT]"]
  LED2 = LED - 5mm [color="Red (633nm)" current=0.030A package="5 mm [THT]"]
  R46 = Resistor [tolerance=±5% power=0.25W resistance=450 package=THT]
  VM1 = Multimeter (DC Voltage)
  S8 = Toggle Switch [package=THT]
  R47 = Resistor [tolerance=±5% power=0.25W resistance=10k package=THT]
  R48 = Resistor [tolerance=±5% power=0.25W resistance=10k package=THT]
  S1 = Toggle Switch [package=THT]
  S10 = Toggle Switch [package=THT]
  S9 = Toggle Switch [package=THT]
  LED3 = LED - 5mm [color="Red (633nm)" current=0.030A package="5 mm [THT]"]
  LED4 = LED - 5mm [color="Red (633nm)" current=0.030A package="5 mm [THT]"]
  Q31 = NPN-Transistor [package="TO92 [THT]"]
  Q32 = NPN-Transistor [package="TO92 [THT]"]
  Q33 = NPN-Transistor [package="TO92 [THT]"]
  Q34 = NPN-Transistor [package="TO92 [THT]"]
  Q35 = NPN-Transistor [package="TO92 [THT]"]
  Q36 = NPN-Transistor [package="TO92 [THT]"]
  Q37 = NPN-Transistor [package="TO92 [THT]"]
  Q38 = NPN-Transistor [package="TO92 [THT]"]
  Q39 = NPN-Transistor [package="TO92 [THT]"]
  Q40 = NPN-Transistor [package="TO92 [THT]"]
  Q41 = NPN-Transistor [package="TO92 [THT]"]
  Q42 = NPN-Transistor [package="TO92 [THT]"]
  Q43 = NPN-Transistor [package="TO92 [THT]"]
  Q44 = NPN-Transistor [package="TO92 [THT]"]
  Q45 = NPN-Transistor [package="TO92 [THT]"]
  Q46 = NPN-Transistor [package="TO92 [THT]"]
  Q47 = NPN-Transistor [package="TO92 [THT]"]
  Q48 = NPN-Transistor [package="TO92 [THT]"]
  Q49 = NPN-Transistor [package="TO92 [THT]"]
  Q50 = NPN-Transistor [package="TO92 [THT]"]
  Q51 = NPN-Transistor [package="TO92 [THT]"]
  Q52 = NPN-Transistor [package="TO92 [THT]"]
  Q53 = NPN-Transistor [package="TO92 [THT]"]
  Q54 = NPN-Transistor [package="TO92 [THT]"]
  Q55 = NPN-Transistor [package="TO92 [THT]"]
  Q56 = NPN-Transistor [package="TO92 [THT]"]
  Q57 = NPN-Transistor [package="TO92 [THT]"]
  Q58 = NPN-Transistor [package="TO92 [THT]"]
  Q59 = NPN-Transistor [package="TO92 [THT]"]
  R49 = Resistor [tolerance=±5% power=0.25W resistance=10k package=THT]
  R50 = Resistor [tolerance=±5% power=0.25W resistance=10k package=THT]
  R51 = Resistor [tolerance=±5% power=0.25W resistance=10k package=THT]
  R52 = Resistor [tolerance=±5% power=0.25W resistance=10k package=THT]
  R53 = Resistor [tolerance=±5% power=0.25W resistance=10k package=THT]
  R54 = Resistor [tolerance=±5% power=0.25W resistance=10k package=THT]
  R55 = Resistor [tolerance=±5% power=0.25W resistance=10k package=THT]
  R56 = Resistor [tolerance=±5% power=0.25W resistance=10k package=THT]
  R57 = Resistor [tolerance=±5% power=0.25W resistance=10k package=THT]
  R58 = Resistor [tolerance=±5% power=0.25W resistance=10k package=THT]
  R59 = Resistor [tolerance=±5% power=0.25W resistance=450 package=THT]
  R60 = Resistor [tolerance=±5% power=0.25W resistance=450 package=THT]
  R61 = Resistor [tolerance=±5% power=0.25W resistance=4.7k package=THT]
  R62 = Resistor [tolerance=±5% power=0.25W resistance=4.7k package=THT]
  R63 = Resistor [tolerance=±5% power=0.25W resistance=4.7k package=THT]
  R64 = Resistor [tolerance=±5% power=0.25W resistance=4.7k package=THT]
  R65 = Resistor [tolerance=±5% power=0.25W resistance=4.7k package=THT]
  R66 = Resistor [tolerance=±5% power=0.25W resistance=4.7k package=THT]
  R67 = Resistor [tolerance=±5% power=0.25W resistance=4.7k package=THT]
  R68 = Resistor [tolerance=±5% power=0.25W resistance=4.7k package=THT]
  R69 = Resistor [tolerance=±5% power=0.25W resistance=4.7k package=THT]
  R70 = Resistor [tolerance=±5% power=0.25W resistance=4.7k package=THT]
  R71 = Resistor [tolerance=±5% power=0.25W resistance=4.7k package=THT]
  R72 = Resistor [tolerance=±5% power=0.25W resistance=4.7k package=THT]
  R73 = Resistor [tolerance=±5% power=0.25W resistance=4.7k package=THT]
  R74 = Resistor [tolerance=±5% power=0.25W resistance=4.7k package=THT]
  R75 = Resistor [tolerance=±5% power=0.25W resistance=4.7k package=THT]
  R76 = Resistor [tolerance=±5% power=0.25W resistance=10k package=THT]
  R77 = Resistor [tolerance=±5% power=0.25W resistance=10k package=THT]
  R78 = Resistor [tolerance=±5% power=0.25W resistance=10k package=THT]
  R79 = Resistor [tolerance=±5% power=0.25W resistance=10k package=THT]
  R80 = Resistor [tolerance=±5% power=0.25W resistance=10k package=THT]
  R81 = Resistor [tolerance=±5% power=0.25W resistance=10k package=THT]
  R82 = Resistor [tolerance=±5% power=0.25W resistance=10k package=THT]
  R83 = Resistor [tolerance=±5% power=0.25W resistance=10k package=THT]
  R84 = Resistor [tolerance=±5% power=0.25W resistance=10k package=THT]
  R85 = Resistor [tolerance=±5% power=0.25W resistance=10k package=THT]
  R86 = Resistor [tolerance=±5% power=0.25W resistance=10k package=THT]
  R87 = Resistor [tolerance=±5% power=0.25W resistance=10k package=THT]
  R88 = Resistor [tolerance=±5% power=0.25W resistance=10k package=THT]
  R89 = Resistor [tolerance=±5% power=0.25W resistance=10k package=THT]
  LED5 = LED - 5mm [color="Red (633nm)" current=0.030A package="5 mm [THT]"]
  LED6 = LED - 5mm [color="Red (633nm)" current=0.030A package="5 mm [THT]"]
  Q60 = NPN-Transistor [package="TO92 [THT]"]
  Q61 = NPN-Transistor [package="TO92 [THT]"]
  Q62 = NPN-Transistor [package="TO92 [THT]"]
  Q63 = NPN-Transistor [package="TO92 [THT]"]
  Q64 = NPN-Transistor [package="TO92 [THT]"]
  Q65 = NPN-Transistor [package="TO92 [THT]"]
  Q66 = NPN-Transistor [package="TO92 [THT]"]
  Q67 = NPN-Transistor [package="TO92 [THT]"]
  Q68 = NPN-Transistor [package="TO92 [THT]"]
  Q69 = NPN-Transistor [package="TO92 [THT]"]
  Q70 = NPN-Transistor [package="TO92 [THT]"]
  Q71 = NPN-Transistor [package="TO92 [THT]"]
  Q72 = NPN-Transistor [package="TO92 [THT]"]
  Q73 = NPN-Transistor [package="TO92 [THT]"]
  Q74 = NPN-Transistor [package="TO92 [THT]"]
  Q75 = NPN-Transistor [package="TO92 [THT]"]
  Q76 = NPN-Transistor [package="TO92 [THT]"]
  Q77 = NPN-Transistor [package="TO92 [THT]"]
  Q78 = NPN-Transistor [package="TO92 [THT]"]
  Q79 = NPN-Transistor [package="TO92 [THT]"]
  Q80 = NPN-Transistor [package="TO92 [THT]"]
  Q81 = NPN-Transistor [package="TO92 [THT]"]
  Q82 = NPN-Transistor [package="TO92 [THT]"]
  Q83 = NPN-Transistor [package="TO92 [THT]"]
  Q84 = NPN-Transistor [package="TO92 [THT]"]
  Q85 = NPN-Transistor [package="TO92 [THT]"]
  Q86 = NPN-Transistor [package="TO92 [THT]"]
  Q87 = NPN-Transistor [package="TO92 [THT]"]
  Q88 = NPN-Transistor [package="TO92 [THT]"]
  R90 = Resistor [tolerance=±5% power=0.25W resistance=10k package=THT]
  R91 = Resistor [tolerance=±5% power=0.25W resistance=10k package=THT]
  R92 = Resistor [tolerance=±5% power=0.25W resistance=10k package=THT]
  R93 = Resistor [tolerance=±5% power=0.25W resistance=10k package=THT]
  R94 = Resistor [tolerance=±5% power=0.25W resistance=10k package=THT]
  R95 = Resistor [tolerance=±5% power=0.25W resistance=10k package=THT]
  R96 = Resistor [tolerance=±5% power=0.25W resistance=10k package=THT]
  R97 = Resistor [tolerance=±5% power=0.25W resistance=10k package=THT]
  R98 = Resistor [tolerance=±5% power=0.25W resistance=10k package=THT]
  R99 = Resistor [tolerance=±5% power=0.25W resistance=10k package=THT]
  R100 = Resistor [tolerance=±5% power=0.25W resistance=450 package=THT]
  R101 = Resistor [tolerance=±5% power=0.25W resistance=450 package=THT]
  R102 = Resistor [tolerance=±5% power=0.25W resistance=4.7k package=THT]
  R103 = Resistor [tolerance=±5% power=0.25W resistance=4.7k package=THT]
  R104 = Resistor [tolerance=±5% power=0.25W resistance=4.7k package=THT]
  R105 = Resistor [tolerance=±5% power=0.25W resistance=4.7k package=THT]
  R106 = Resistor [tolerance=±5% power=0.25W resistance=4.7k package=THT]
  R107 = Resistor [tolerance=±5% power=0.25W resistance=4.7k package=THT]
  R108 = Resistor [tolerance=±5% power=0.25W resistance=4.7k package=THT]
  R109 = Resistor [tolerance=±5% power=0.25W resistance=4.7k package=THT]
  R110 = Resistor [tolerance=±5% power=0.25W resistance=4.7k package=THT]
  R111 = Resistor [tolerance=±5% power=0.25W resistance=4.7k package=THT]
  R112 = Resistor [tolerance=±5% power=0.25W resistance=4.7k package=THT]
  R113 = Resistor [tolerance=±5% power=0.25W resistance=4.7k package=THT]
  R114 = Resistor [tolerance=±5% power=0.25W resistance=4.7k package=THT]
  R115 = Resistor [tolerance=±5% power=0.25W resistance=4.7k package=THT]
  R116 = Resistor [tolerance=±5% power=0.25W resistance=4.7k package=THT]
  R117 = Resistor [tolerance=±5% power=0.25W resistance=10k package=THT]
  R118 = Resistor [tolerance=±5% power=0.25W resistance=10k package=THT]
  R119 = Resistor [tolerance=±5% power=0.25W resistance=10k package=THT]
  R120 = Resistor [tolerance=±5% power=0.25W resistance=10k package=THT]
  R121 = Resistor [tolerance=±5% power=0.25W resistance=10k package=THT]
  R122 = Resistor [tolerance=±5% power=0.25W resistance=10k package=THT]
  R123 = Resistor [tolerance=±5% power=0.25W resistance=10k package=THT]
  R124 = Resistor [tolerance=±5% power=0.25W resistance=10k package=THT]
  R125 = Resistor [tolerance=±5% power=0.25W resistance=10k package=THT]
  R126 = Resistor [tolerance=±5% power=0.25W resistance=10k package=THT]
  R127 = Resistor [tolerance=±5% power=0.25W resistance=10k package=THT]
  R128 = Resistor [tolerance=±5% power=0.25W resistance=10k package=THT]
  R129 = Resistor [tolerance=±5% power=0.25W resistance=10k package=THT]
  R130 = Resistor [tolerance=±5% power=0.25W resistance=10k package=THT]

nets:
  N1: Q1.E, R1.Pin_1
  N2: Q1.B, R3.Pin_1
  N3: VCC2.-, Q2.E, Q4.E, Q7.E, Q8.E, Q10.E, Q13.E, Q15.E, Q16.E, Q17.E, Q19.E, Q20.E, Q21.E, Q22.E, R35.Pin_1, Q25.E, Q26.E, Q28.E, Q29.E, Q30.E, VM1.COM_Probe, Q60.E, Q61.E, Q67.E, Q68.E, Q69.E, Q70.E, Q71.E, Q73.E, Q74.E, Q75.E, Q77.E, Q78.E, Q80.E, Q81.E, Q82.E, Q84.E, Q87.E, Q88.E, R122.Pin_1
  N4: VCC2.+, S2.COM, S3.COM, S4.COM, S5.COM, S6.COM, S7.COM, S11.COM, S12.COM, S13.COM, S14.COM, S15.COM, S16.COM, S17.COM, R8.Pin_1, R9.Pin_1, R10.Pin_1, R17.Pin_0, R18.Pin_0, R19.Pin_0, R23.Pin_1, R25.Pin_1, R30.Pin_0, R31.Pin_0, R36.Pin_1, R37.Pin_1, R40.Pin_0, R41.Pin_0, R42.Pin_0, R45.Pin_1, R46.Pin_1, S8.COM, S1.COM, S10.COM, S9.COM, R100.Pin_1, R101.Pin_1, R102.Pin_0, R103.Pin_0, R104.Pin_1, R105.Pin_1, R106.Pin_0, R107.Pin_0, R108.Pin_1, R109.Pin_1, R110.Pin_0, R111.Pin_0, R112.Pin_1, R113.Pin_1, R114.Pin_0, R115.Pin_0, R116.Pin_1
  N5: Q2.B, R5.Pin_1
  N6: Q2.C, Q3.E
  N7: Q3.B, R6.Pin_1
  N8: Q3.C, Q4.B, R8.Pin_0
  N9: R5.Pin_0, R13.Pin_0, S10.L1
  N10: R6.Pin_0, R14.Pin_1, R16.Pin_0, R21.Pin_1, R28.Pin_1, VM1.V_Probe, S9.L1
  N11: Q4.C, Q6.E, Q5.E
  N12: Q6.B, R14.Pin_0
  N13: Q6.C, Q7.B, R9.Pin_0, Q5.C
  N14: Q7.C, R10.Pin_0, R24.Pin_1, R38.Pin_1, R43.Pin_0
  N15: Q5.B, R13.Pin_1
  N16: R15.Pin_0, R20.Pin_0, R27.Pin_1, Q25.C, R41.Pin_1
  N17: R15.Pin_1, Q8.B
  N18: R16.Pin_1, Q9.B
  N19: R17.Pin_1, Q9.C, Q10.B
  N20: Q8.C, Q9.E
  N21: Q10.C, Q11.E, Q12.E
  N22: Q11.B, R20.Pin_1
  N23: Q11.C, Q12.C, Q13.B, R19.Pin_1
  N24: Q12.B, R21.Pin_0
  N25: Q13.C, R18.Pin_1, R47.Pin_0
  N26: Q14.E, Q16.C
  N27: Q14.B, R22.Pin_0
  N28: Q14.C, R23.Pin_0, R26.Pin_0
  N29: Q15.B, R26.Pin_1
  N30: Q15.C, R25.Pin_0, R33.Pin_0
  N31: Q16.B, R24.Pin_0
  N32: R22.Pin_1, R39.Pin_0, R44.Pin_0, S1.L1
  N33: Q17.B, R28.Pin_0
  N34: Q17.C, Q18.E
  N35: Q18.B, R27.Pin_0
  N36: Q18.C, R29.Pin_0, R31.Pin_1
  N37: R29.Pin_1, Q19.B
  N38: Q19.C, R30.Pin_1, R32.Pin_1
  N39: Q20.B, R32.Pin_0
  N40: Q20.C, Q21.C, R34.Pin_0, R35.Pin_0, R36.Pin_0
  N41: Q21.B, R33.Pin_1
  N42: Q22.B, R34.Pin_1
  N43: Q22.C, R37.Pin_0, R48.Pin_0
  N44: Q23.E, Q24.E, Q26.C
  N45: Q23.B, R38.Pin_0
  N46: Q23.C, Q24.C, Q25.B, R40.Pin_1
  N47: Q24.B, R39.Pin_1
  N48: Q26.B, Q27.C, R42.Pin_1
  N49: Q27.E, Q28.C
  N50: Q27.B, R43.Pin_1
  N51: Q28.B, R44.Pin_1
  N52: R45.Pin_0, LED1.anode
  N53: LED1.cathode, Q29.C
  N54: Q29.B, R47.Pin_1
  N55: Q30.B, R48.Pin_1
  N56: Q30.C, LED2.cathode
  N57: LED2.anode, R46.Pin_0
  N58: LED3.cathode, Q31.C
  N59: LED3.anode, R59.Pin_0
  N60: LED4.cathode, Q32.C
  N61: LED4.anode, R60.Pin_0
  N62: Q31.E, Q32.E, Q38.E, Q39.E, Q40.E, Q41.E, Q42.E, Q44.E, Q45.E, Q46.E, Q48.E, Q49.E, Q51.E, Q52.E, Q53.E, Q55.E, Q58.E, Q59.E, R81.Pin_1
  N63: Q31.B, R77.Pin_1
  N64: Q32.B, R78.Pin_1
  N65: Q33.E, Q34.E, Q51.C
  N66: Q33.B, R56.Pin_1
  N67: Q33.C, Q34.C, Q38.B, R62.Pin_1
  N68: Q34.B, R49.Pin_0
  N69: Q35.E, Q36.E, Q52.C
  N70: Q35.B, R54.Pin_0
  N71: Q35.C, Q36.C, Q48.B, R69.Pin_1
  N72: Q36.B, R57.Pin_1
  N73: Q37.E, Q50.E, Q53.C
  N74: Q37.B, R58.Pin_1
  N75: Q37.C, Q49.B, Q50.C, R72.Pin_0
  N76: Q38.C, R52.Pin_1, R57.Pin_0, R61.Pin_1, R88.Pin_0
  N77: Q39.B, R82.Pin_1
  N78: Q39.C, R63.Pin_0, R77.Pin_0
  N79: Q40.B, R50.Pin_1
  N80: Q40.C, Q41.C, R64.Pin_0, R81.Pin_0, R82.Pin_0
  N81: Q41.B, R51.Pin_0
  N82: Q42.B, R83.Pin_1
  N83: Q42.C, R51.Pin_1, R66.Pin_1
  N84: Q43.E, Q44.C
  N85: Q43.B, R52.Pin_0
  N86: Q43.C, R65.Pin_1, R83.Pin_0
  N87: Q44.B, R84.Pin_0
  N88: Q45.B, R86.Pin_0
  N89: Q45.C, Q47.E
  N90: Q46.B, R85.Pin_1
  N91: Q46.C, R50.Pin_0, R67.Pin_0
  N92: Q47.B, R53.Pin_0
  N93: Q47.C, R68.Pin_0, R85.Pin_0
  N94: Q48.C, R70.Pin_1, R78.Pin_0
  N95: Q49.C, R49.Pin_1, R71.Pin_0, R80.Pin_0, R86.Pin_1
  N96: Q50.B, R55.Pin_0
  N97: Q51.B, Q56.C, R73.Pin_1
  N98: Q52.B, Q57.C, R74.Pin_1
  N99: Q53.B, Q54.C, R75.Pin_0
  N100: Q54.E, Q59.C
  N101: Q54.B, R76.Pin_1
  N102: Q55.B, R79.Pin_1
  N103: Q55.C, Q56.E
  N104: Q56.B, R80.Pin_1
  N105: Q57.E, Q58.C
  N106: Q57.B, R87.Pin_1
  N107: Q58.B, R88.Pin_1
  N108: Q59.B, R89.Pin_1
  N109: R59.Pin_1, R60.Pin_1, R61.Pin_0, R62.Pin_0, R63.Pin_1, R64.Pin_1, R65.Pin_0, R66.Pin_0, R67.Pin_1, R68.Pin_1, R69.Pin_0, R70.Pin_0, R71.Pin_1, R72.Pin_1, R73.Pin_0, R74.Pin_0, R75.Pin_1
  N110: LED5.cathode, Q60.C
  N111: LED5.anode, R100.Pin_0
  N112: LED6.cathode, Q61.C
  N113: LED6.anode, R101.Pin_0
  N114: Q60.B, R118.Pin_1
  N115: Q61.B, R119.Pin_1
  N116: Q62.E, Q63.E, Q80.C
  N117: Q62.B, R97.Pin_1
  N118: Q62.C, Q63.C, Q67.B, R103.Pin_1
  N119: Q63.B, R90.Pin_0
  N120: Q64.E, Q65.E, Q81.C
  N121: Q64.B, R95.Pin_0
  N122: Q64.C, Q65.C, Q77.B, R110.Pin_1
  N123: Q65.B, R98.Pin_1
  N124: Q66.E, Q79.E, Q82.C
  N125: Q66.B, R99.Pin_1
  N126: Q66.C, Q78.B, Q79.C, R113.Pin_0
  N127: Q67.C, R93.Pin_1, R98.Pin_0, R102.Pin_1, R129.Pin_0
  N128: Q68.B, R123.Pin_1
  N129: Q68.C, R104.Pin_0, R118.Pin_0
  N130: Q69.B, R91.Pin_1
  N131: Q69.C, Q70.C, R105.Pin_0, R122.Pin_0, R123.Pin_0
  N132: Q70.B, R92.Pin_0
  N133: Q71.B, R124.Pin_1
  N134: Q71.C, R92.Pin_1, R107.Pin_1
  N135: Q72.E, Q73.C
  N136: Q72.B, R93.Pin_0
  N137: Q72.C, R106.Pin_1, R124.Pin_0
  N138: Q73.B, R125.Pin_0
  N139: Q74.B, R127.Pin_0
  N140: Q74.C, Q76.E
  N141: Q75.B, R126.Pin_1
  N142: Q75.C, R91.Pin_0, R108.Pin_0
  N143: Q76.B, R94.Pin_0
  N144: Q76.C, R109.Pin_0, R126.Pin_0
  N145: Q77.C, R111.Pin_1, R119.Pin_0
  N146: Q78.C, R90.Pin_1, R112.Pin_0, R121.Pin_0, R127.Pin_1
  N147: Q79.B, R96.Pin_0
  N148: Q80.B, Q85.C, R114.Pin_1
  N149: Q81.B, Q86.C, R115.Pin_1
  N150: Q82.B, Q83.C, R116.Pin_0
  N151: Q83.E, Q88.C
  N152: Q83.B, R117.Pin_1
  N153: Q84.B, R120.Pin_1
  N154: Q84.C, Q85.E
  N155: Q85.B, R121.Pin_1
  N156: Q86.E, Q87.C
  N157: Q86.B, R128.Pin_1
  N158: Q87.B, R129.Pin_1
  N159: Q88.B, R130.Pin_1

notes:
  Input A
  Output A
  Number A
  Number B
  Subtract
